# Fritzing sketch AMT103V (saved by Fritzing 0.9.3b)

parts:
  Part1 = Arduino Mega ADK (Rev3)
  CUI-enc1 = AMT103
  CUI-enc2 = AMT103

nets:
  N1: Part1.D19/RX1, CUI-enc2.A
  N2: Part1.D18/TX1, CUI-enc2.B
  N3: Part1.D2_PWM, CUI-enc1.A
  N4: Part1.D3_PWM, CUI-enc1.B

custom parts:
  AMT103: CUI AMT103 Modular incremental encoder. Resolutions 48, 96, 100, 125, 192, 200, 250, 256, 384, 400, 500, 512, 800, 1000, 1024, 2048 either fixed (resolution indicated by part number) or selectable via dip switch. Index output once per revolution. VCC 5V (3.6V min, probably too high for 3.3V operation)
