# Fritzing sketch MPU-6050 Board GY-521 Acelerometro Giroscopio (saved by Fritzing 0.9.3b)

parts:
  Part1 = Arduino Mega ADK (Rev3)
  GY1 = MPU-6050 Board GY-521 [form="♀ (female)" package=THT]

nets:
  N1: Part1.D21/SCL, GY1.pin3
  N2: Part1.D20/SDA, GY1.pin4
  N3: Part1.3V3, GY1.pin1
  N4: Part1.GND, GY1.pin2

custom parts:
  MPU-6050 Board GY-521: Acelerometro y Giroscopio MPU-6050 Board GY-521
